// Logisim project alu.circ as structural Verilog: 4 circuits, main circuit main
module main (
  input  A3,
  input  B3,
  input  A2,
  input  B2,
  input  A1,
  input  B1,
  input  A0,
  input  B0,
  input  C1,
  input  C0
);

  wire control_1_aandb, control_1_add, control_1_aorb, control_1_sub, n74283_1_pin7, n74283_2_pin7,
       not_1_out, not_2_out, not_3_out, not_4_out;
  wire [3:0] controlled_buffer_1_out, log_and_1_c0, log_or_1_c0, n74283_1_pin4, n74283_2_pin4;

  _74283 u_74283_1 (
    .pin1(n74283_1_pin4[1]), .pin2(B1), .pin3(A1), .pin4(n74283_1_pin4[0]), .pin5(A0), .pin6(B0),
    .pin7(n74283_1_pin7), .pin15(B2), .pin14(A2), .pin13(n74283_1_pin4[2]), .pin12(B3), .pin11(A3),
    .pin10(n74283_1_pin4[3]));  // open: pin9
  log_and log_and_1 (
    .B3(B3), .B2(B2), .B1(B1), .B0(B0), .A3(A3), .A2(A2), .A1(A1), .A0(A0), .C3(log_and_1_c0[3]),
    .C2(log_and_1_c0[2]), .C1(log_and_1_c0[1]), .C0(log_and_1_c0[0]));
  log_or log_or_1 (
    .B3(B3), .B2(B2), .B1(B1), .B0(B0), .A3(A3), .A2(A2), .A1(A1), .A0(A0), .C3(log_or_1_c0[3]),
    .C2(log_or_1_c0[2]), .C1(log_or_1_c0[1]), .C0(log_or_1_c0[0]));
  not not_1 (not_1_out, B3);
  not not_2 (not_2_out, B2);
  not not_3 (not_3_out, B1);
  not not_4 (not_4_out, B0);
  _74283 u_74283_2 (
    .pin1(n74283_2_pin4[1]), .pin2(not_3_out), .pin3(A1), .pin4(n74283_2_pin4[0]), .pin5(A0),
    .pin6(not_4_out), .pin7(n74283_2_pin7), .pin15(not_2_out), .pin14(A2), .pin13(n74283_2_pin4[2]),
    .pin12(A3), .pin11(not_1_out), .pin10(n74283_2_pin4[3]));  // open: pin9
  control control_1 (
    .C1(C1), .C0(C0), .add(control_1_add), .sub(control_1_sub), .AandB(control_1_aandb), .AorB(control_1_aorb));
  assign controlled_buffer_1_out = control_1_sub ? n74283_2_pin4 : 4'bz;  // Controlled_Buffer controlled_buffer_1
  assign controlled_buffer_1_out = control_1_add ? n74283_1_pin4 : 4'bz;  // Controlled_Buffer controlled_buffer_2
  assign controlled_buffer_1_out = control_1_aandb ? log_and_1_c0 : 4'bz;  // Controlled_Buffer controlled_buffer_3
  assign controlled_buffer_1_out = control_1_aorb ? log_or_1_c0 : 4'bz;  // Controlled_Buffer controlled_buffer_4
  Hex_Digit_Display #(.decimalPoint("false")) hex_digit_display_1 (.value(controlled_buffer_1_out));
  // also tied to GND on the sheet: n74283_1_pin7
  // also tied to VCC on the sheet: n74283_2_pin7
endmodule

module log_and (
  input  B3,
  input  B2,
  input  B1,
  input  B0,
  input  A3,
  input  A2,
  input  A1,
  input  A0,
  output C3,
  output C2,
  output C1,
  output C0
);

  and and_1 (C3, B3, A3);
  and and_2 (C2, B2, A2);
  and and_3 (C1, B1, A1);
  and and_4 (C0, B0, A0);
endmodule

module log_or (
  input  B3,
  input  B2,
  input  B1,
  input  B0,
  input  A3,
  input  A2,
  input  A1,
  input  A0,
  output C3,
  output C2,
  output C1,
  output C0
);

  or or_1 (C3, B3, A3);
  or or_2 (C2, B2, A2);
  or or_3 (C1, B1, A1);
  or or_4 (C0, B0, A0);
endmodule

module control (
  input  C1,
  input  C0,
  output add,
  output sub,
  output AandB,
  output AorB
);

  wire not_1_out, not_2_out;

  not not_1 (not_1_out, C1);
  not not_2 (not_2_out, C0);
  and and_1 (add, not_1_out, not_2_out);
  and and_2 (sub, not_1_out, C0);
  and and_3 (AandB, C1, not_2_out);
  and and_4 (AorB, C1, C0);
endmodule
