// Logisim project cache.circ as structural Verilog: 1 circuit, main circuit main
module main (
  input  [5:0] in_1
);

  wire clock_1_out, nand_1_out, xnor_1_out, xnor_2_out, xnor_3_out;
  wire [2:0] controlled_buffer_1_out, ram_1_dout;

  Clock clock_1 (.out(clock_1_out));
  xnor xnor_1 (xnor_1_out, in_1[3], ram_1_dout[0]);
  assign controlled_buffer_1_out = nand_1_out ? in_1[5:3] : 3'bz;  // Controlled_Buffer controlled_buffer_1
  xnor xnor_2 (xnor_2_out, in_1[4], ram_1_dout[1]);
  nand nand_1 (nand_1_out, xnor_1_out, xnor_2_out, xnor_3_out);
  RAM #(.addrWidth(3), .dataWidth(3), .enables("line")) ram_1 (
    .addr(in_1[2:0]), .we(nand_1_out), .clk(clock_1_out), .din(controlled_buffer_1_out), .dout(ram_1_dout));
  xnor xnor_3 (xnor_3_out, in_1[5], ram_1_dout[2]);
  _7_Segment_Display #(.decimalPoint("false")) u_7_segment_display_1 (
    .g(1'b0), .f(nand_1_out), .a(nand_1_out), .b(1'b1), .e(nand_1_out), .d(nand_1_out), .c(1'b1));
endmodule
