// Logisim project cpu_mem.circ as structural Verilog: 4 circuits, main circuit RAM1Kx4
module main (
  input  in_1,
  input  [15:0] in_2,
  input  in_3
);

  wire and_1_out, cpu_1_notmerq, cpu_1_notwr, n74138_1_pin10, n74138_1_pin11, not_1_out, not_2_out, not_3_out;
  wire [7:0] cpu_1_data;
  wire [15:0] cpu_1_address;

  cpu cpu_1 (
    .MERQin(in_1), .Datain(cpu_1_data), .Addressin(in_2), .notWRin(in_3), .notMERQ(cpu_1_notmerq),
    .Data(cpu_1_data), .Address(cpu_1_address), .notWR(cpu_1_notwr));
  ROM2Kx8 rom2kx8_1 (
    .A0(cpu_1_address[9]), .A1(cpu_1_address[8]), .A2(cpu_1_address[7]), .A3(cpu_1_address[6]),
    .A4(cpu_1_address[5]), .A5(cpu_1_address[4]), .A6(cpu_1_address[3]), .A7(cpu_1_address[2]),
    .A8(cpu_1_address[1]), .A9(cpu_1_address[0]), .A10(cpu_1_address[10]), .CS(n74138_1_pin11),
    .D5(cpu_1_data[2]), .D4(cpu_1_data[3]), .D3(cpu_1_data[4]), .D2(cpu_1_data[5]), .D1(cpu_1_data[6]),
    .D0(cpu_1_data[7]), .D7(cpu_1_data[0]), .D6(cpu_1_data[1]));
  _74138 u_74138_1 (
    .pin1(cpu_1_address[11]), .pin2(cpu_1_address[12]), .pin3(cpu_1_address[13]), .pin4(cpu_1_address[15]),
    .pin5(cpu_1_notmerq), .pin6(cpu_1_address[14]), .pin11(n74138_1_pin11), .pin10(n74138_1_pin10));  // open: pin7, pin15, pin14, pin13, pin12, pin9
  not not_1 (not_1_out, cpu_1_address[10]);
  not not_2 (not_2_out, n74138_1_pin10);
  and and_1 (and_1_out, not_1_out, not_2_out);
  not not_3 (not_3_out, and_1_out);
  RAM1Kx4 ram1kx4_1 (
    .WR(cpu_1_notwr), .CS(not_3_out), .A9(cpu_1_address[0]), .A8(cpu_1_address[1]), .A7(cpu_1_address[2]),
    .A6(cpu_1_address[3]), .A5(cpu_1_address[4]), .A4(cpu_1_address[5]), .A3(cpu_1_address[6]),
    .A2(cpu_1_address[7]), .A1(cpu_1_address[8]), .A0(cpu_1_address[9]), .D1(cpu_1_data[2]),
    .D0(cpu_1_data[3]), .D3(cpu_1_data[0]), .D2(cpu_1_data[1]));
  RAM1Kx4 ram1kx4_2 (
    .WR(cpu_1_notwr), .CS(not_3_out), .A9(cpu_1_address[0]), .A8(cpu_1_address[1]), .A7(cpu_1_address[2]),
    .A6(cpu_1_address[3]), .A5(cpu_1_address[4]), .A4(cpu_1_address[5]), .A3(cpu_1_address[6]),
    .A2(cpu_1_address[7]), .A1(cpu_1_address[8]), .A0(cpu_1_address[9]), .D1(cpu_1_data[6]),
    .D0(cpu_1_data[7]), .D3(cpu_1_data[4]), .D2(cpu_1_data[5]));

  // Notes on the sheet:
  //   in_2: initial=0x6800
  //   WR
endmodule

module RAM1Kx4 (
  input  A9,
  input  A8,
  input  A7,
  input  A6,
  input  A5,
  input  A4,
  input  A3,
  input  A2,
  input  A1,
  input  A0,
  input  WR,
  input  CS,
  output D3,
  output D2,
  output D1,
  output D0
);

  wire and_1_out, and_2_out, clock_1_out, not_1_out, not_2_out, not_3_out;

  not not_1 (not_1_out, WR);
  not not_2 (not_2_out, not_1_out);
  not not_3 (not_3_out, CS);
  and and_1 (and_1_out, not_1_out, not_3_out);
  and and_2 (and_2_out, not_2_out, not_3_out);
  RAM #(.addrWidth(10), .dataWidth(4), .databus("bidir"), .enables("line")) ram_1 (
    .addr({A9, A8, A7, A6, A5, A4, A3, A2, A1, A0}), .we(and_1_out), .oe(and_2_out), .clk(clock_1_out),
    .data({D3, D2, D1, D0}));
  Clock clock_1 (.out(clock_1_out));
endmodule

module ROM2Kx8 (
  input  A0,
  input  A1,
  input  A2,
  input  A3,
  input  A4,
  input  A5,
  input  A6,
  input  A7,
  input  A8,
  input  A9,
  input  A10,
  input  CS,
  output D7,
  output D6,
  output D5,
  output D4,
  output D3,
  output D2,
  output D1,
  output D0
);

  wire not_1_out;
  wire [10:0] controlled_buffer_1_out;

  not not_1 (not_1_out, CS);
  assign controlled_buffer_1_out = not_1_out ? {A10, A9, A8, A7, A6, A5, A4, A3, A2, A1, A0} : 11'bz;  // Controlled_Buffer controlled_buffer_1
  ROM #(.addrWidth(11)) rom_1 (.addr(controlled_buffer_1_out), .data({D7, D6, D5, D4, D3, D2, D1, D0}));
endmodule

module cpu (
  input  MERQin,
  input  [7:0] Datain,
  input  [15:0] Addressin,
  input  notWRin,
  output notMERQ,
  output [7:0] Data,
  output [15:0] Address,
  output notWR
);

  wire not_1_out;

  assign Data = not_1_out ? Datain : 8'bz;  // Controlled_Buffer controlled_buffer_1
  not not_1 (not_1_out, notWRin);

  assign Address = Addressin;
  assign notMERQ = MERQin;
  assign notWR = notWRin;

  // Notes on the sheet:
  //   Addressin: initial=0x6800
endmodule
