// Logisim project link.circ as structural Verilog: 1 circuit, main circuit main
module main (
);

  wire and_1_out, and_2_out, and_3_out, and_4_out, and_5_out, and_6_out, and_7_out, and_8_out, and_9_out,
       and_10_out, and_11_out, and_12_out, and_13_out, and_14_out, and_15_out, and_16_out, and_17_out,
       clock_1_out, d_ff_1_q, d_ff_2_q, d_ff_2_qn, d_ff_3_q, d_ff_3_qn, d_ff_4_q, d_ff_4_qn, d_ff_5_q,
       d_ff_5_qn, not_1_out, or_1_out, or_2_out, or_3_out, or_4_out, or_5_out, or_6_out, or_7_out, or_8_out,
       or_9_out, or_10_out, or_11_out, or_12_out, undriven;

  not not_1 (not_1_out, or_1_out);
  and and_1 (and_1_out, not_1_out, or_2_out);
  D_Flip_Flop d_ff_1 (.D(and_1_out), .clk(clock_1_out), .Q(d_ff_1_q));  // open: Qn, preset, reset
  Clock clock_1 (.out(clock_1_out));
  or or_1 (or_1_out, or_4_out, and_4_out);
  and and_2 (and_2_out, 1'b0, and_3_out);
  or or_2 (or_2_out, or_5_out, d_ff_2_q);
  D_Flip_Flop d_ff_2 (.D(1'b0), .clk(clock_1_out), .Q(d_ff_2_q), .Qn(d_ff_2_qn));  // open: preset, reset
  and and_3 (and_3_out, 1'b0, d_ff_1_q);
  LED led_1 (.in(and_3_out));
  and and_4 (and_4_out, d_ff_1_q, d_ff_2_q);
  and and_5 (and_5_out, d_ff_2_qn, d_ff_1_q);
  or or_3 (or_3_out, and_2_out, 1'b0);
  or or_4 (or_4_out, or_7_out, and_8_out);
  or or_5 (or_5_out, or_8_out, d_ff_3_q);
  D_Flip_Flop d_ff_3 (.D(1'b1), .clk(clock_1_out), .Q(d_ff_3_q), .Qn(d_ff_3_qn));  // open: preset, reset
  and and_6 (and_6_out, 1'b1, and_7_out);
  and and_7 (and_7_out, 1'b1, and_5_out);
  LED led_2 (.in(and_7_out));
  and and_8 (and_8_out, and_5_out, d_ff_3_q);
  or or_6 (or_6_out, and_6_out, or_3_out);
  or or_7 (or_7_out, or_10_out, and_11_out);
  and and_9 (and_9_out, d_ff_3_qn, and_5_out);
  or or_8 (or_8_out, or_11_out, d_ff_4_q);
  D_Flip_Flop d_ff_4 (.D(1'b0), .clk(clock_1_out), .Q(d_ff_4_q), .Qn(d_ff_4_qn));  // open: preset, reset
  and and_10 (and_10_out, 1'b0, and_12_out);
  and and_11 (and_11_out, and_9_out, d_ff_4_q);
  and and_12 (and_12_out, 1'b0, and_9_out);
  LED led_3 (.in(and_12_out));
  or or_9 (or_9_out, and_10_out, or_6_out);
  and and_13 (and_13_out, d_ff_4_qn, and_9_out);
  or or_10 (or_10_out, 1'b0, and_16_out);
  or or_11 (or_11_out, undriven, d_ff_5_q);
  D_Flip_Flop d_ff_5 (.D(1'b1), .clk(clock_1_out), .Q(d_ff_5_q), .Qn(d_ff_5_qn));  // open: preset, reset
  and and_14 (and_14_out, 1'b1, and_13_out);
  LED led_4 (.in(and_14_out));
  and and_15 (and_15_out, 1'b1, and_14_out);
  and and_16 (and_16_out, and_13_out, d_ff_5_q);
  and and_17 (and_17_out, d_ff_5_qn, and_13_out);
  or or_12 (or_12_out, and_15_out, or_9_out);

  // Notes on the sheet:
  //   BG
  //   BR
  //   BS
  //   数据线
endmodule
